# Fritzing sketch arduino_esp_4cambien (saved by Fritzing 0.9.3b)

parts:
  Part2 = Arduino Uno (Rev3)
  A2 = tds-sensor-meter-v1.0_1
  U3 = Turbidity Sensor Probe [package=THT]
  U4 = DFRobot SEN0189 [package=THT]
  DS2 = DS18B20 1-Wire Temperature Sensor Probe
  U5 = NodeMCU V1.0
  A3 = Dissolved Oxygen meter
  M2 = PH meter with sensor in breadboard [package=THT]

nets:
  N1: Part2.A0, M2.pin1
  N2: Part2.A1, A2.pin1
  N3: Part2.A2, U4.P1_1
  N4: Part2.A3, A3.pin3
  GND: Part2.GND, A2.pin3, U4.P1_3, DS2.GND, U5.GND, A3.pin1, M2.pin3
  N5: Part2.D0/RX, U5.TX
  N6: Part2.D1/TX, U5.RX
  N7: Part2.D4, DS2.DQ
  5V: Part2.5V, A2.pin2, U4.P1_2, DS2.VDD, U5.Vin, A3.pin2, M2.pin2
  N8: U3.pin1, U4.P2_1
  N9: U3.pin2, U4.P2_2
  N10: U3.VCC, U4.P2_3

custom parts:
  : TDS Meter V1.0 Development Board Water Meter Filter Measuring Water Sensor Module.
  Turbidity Sensor Probe: Turbidity sensor probe to the DFRobot measure module.
  DFRobot SEN0189: Turbidity sensor of DFRobot SEN0189
  NodeMCU V1.0: ESP8266 based NodeMCU
  Dissolved Oxygen meter: DFrobot Dissolved Oxygen meter (SKU SEN0237A)
  PH meter with sensor in breadboard: DFrobot PH meter (SKU SEN0161)
